# Fritzing sketch sketch (saved by Fritzing 0.9.2b)
breadboards: 1

parts:
  Part1 = Arduino Uno (Rev3)
  U1 = LCD-16X2 [package=lcd-16x2_noholes]
  RHT1 = Humidity and Temperature Sensor RHT03
  S1 = Momentary Switch [package=ksa_sealed_tac_switch]  # not connected

nets:
  N1: Part1.A0, RHT1.Data-signal
  N2: Part1.D11_PWM/MOSI, U1.E
  N3: Part1.D12/MISO, U1.RS
  N4: Part1.D2, U1.DB7
  N5: Part1.D3_PWM, U1.DB6
  N6: Part1.D4, U1.DB5
  N7: Part1.D5_PWM, U1.DB4
  5V: Part1.5V, RHT1.Vcc
  N8: Part1.GND, RHT1.GND_1
